// Logisim project CPU.circ as structural Verilog: 1 circuit, main circuit main
module main (
);

  wire clk_out, n7404_1_pin2, n7404_1_pin4, n7404_1_pin6, n7404_1_pin8, n7404_1_pin10, n7404_1_pin11,
       n7404_1_pin12, n7404_1_pin13, n7404_2_p2, n7408_1_pin2, n7408_1_pin3, n7408_1_pin4, n7408_1_pin5,
       n7408_1_pin6, n7408_2_pin3, n7408_2_pin6, n7408_2_pin8, n7408_2_pin11, n7408_3_pin3, n7408_3_pin6,
       n7408_3_pin11, n7432_1_p3, n7432_2_pin6, n7432_3_pin1, n7432_3_pin2, n7432_3_pin3, n7432_3_pin5,
       n7432_3_pin6, n7432_3_pin12, n7432_3_pin13, n7432_4_pin1, n7432_4_pin2, n7432_4_pin3, n7432_4_pin6,
       n7432_4_pin11, n7432_4_pin12, n7432_4_pin13, n74175_1_pin2, n74175_1_pin9, n74175_1_pin13, reset_out;
  wire [7:0] pc_q, pc_q_2, pc_q_3, pc_q_4;
  wire [15:0] registerA_q, registerA_q_2;
  wire [31:0] adder_1_out, adder_2_out, and_1_out, and_2_out, and_3_out, bit_extender_1_out,
       bit_extender_2_out, bit_extender_3_out, bit_extender_4_out, bit_extender_5_out,
       controlled_buffer_2_out, multiplexer_1_out, multiplexer_2_out, multiplexer_3_out, multiplexer_4_out,
       n7432_6_pin5, ram_1_data, registerD_q, registerM_q, rom_1_data, xor_1_out, xor_2_out;

  RAM #(.addrWidth(16), .clearpin("true"), .dataWidth(32), .databus("bidir")) ram_1 (
    .addr(registerA_q), .we(n7408_2_pin8), .oe(n74175_1_pin2), .clk(n7404_1_pin8), .data(ram_1_data),
    .clr(reset_out));
  ROM #(.addrWidth(24), .dataWidth(32)) rom_1 (.addr({pc_q_3, pc_q_2, pc_q}), .data(rom_1_data));
  assign ram_1_data = n7408_1_pin4 ? n7432_6_pin5 : 32'bz;  // Controlled_Buffer controlled_buffer_1
  Clock clk (.out(clk_out));
  _7404 u_7404_1 (
    .pin1(rom_1_data[31]), .pin2(n7404_1_pin2), .pin3(rom_1_data[11]), .pin4(n7404_1_pin4),
    .pin5(rom_1_data[9]), .pin6(n7404_1_pin6), .pin13(n7404_1_pin13), .pin12(n7404_1_pin12),
    .pin11(n7404_1_pin11), .pin10(n7404_1_pin10), .pin9(clk_out), .pin8(n7404_1_pin8));
  _7408 u_7408_1 (
    .pin1(rom_1_data[31]), .pin2(n7408_1_pin2), .pin3(n7408_1_pin3), .pin4(n7408_1_pin4),
    .pin5(n7408_1_pin5), .pin6(n7408_1_pin6));  // open: pin13, pin12, pin11, pin10, pin9, pin8
  Button reset (.out(reset_out));
  // _7404 7404_2: pin names not known; wires that end beside it: reset_out, n7404_2_p2, 1'b0, 1'b1
  Register #(.width(32)) pc (
    .D(multiplexer_1_out), .en(n7408_1_pin6), .clk(clk_out), .Q({pc_q_4, pc_q_3, pc_q_2, pc_q}),
    .clr(reset_out));
  _74175 u_74175_1 (
    .pin1(n7404_2_p2), .pin2(n74175_1_pin2), .pin3(n7408_1_pin4), .pin4(n7408_1_pin4), .pin15(n7408_1_pin5),
    .pin13(n74175_1_pin13), .pin9(n74175_1_pin9));  // open: pin5, pin6, pin7, pin14, pin12, pin11, pin10
  // _7432 7432_1: pin names not known; wires that end beside it: n7404_1_pin2, rom_1_data[5], n7432_1_p3, 1'b0, 1'b1
  assign controlled_buffer_2_out = n74175_1_pin2 ? ram_1_data : 32'bz;  // Controlled_Buffer controlled_buffer_2
  _7408 u_7408_2 (
    .pin1(rom_1_data[4]), .pin2(rom_1_data[31]), .pin3(n7408_2_pin3), .pin4(rom_1_data[31]),
    .pin5(rom_1_data[3]), .pin6(n7408_2_pin6), .pin13(n7432_1_p3), .pin12(n7408_1_pin4),
    .pin11(n7408_2_pin11), .pin10(n7408_1_pin4), .pin9(n7408_2_pin6), .pin8(n7408_2_pin8));
  Clock clock_1 (.out(n74175_1_pin9));
  _7408 u_7408_3 (
    .pin1(rom_1_data[2]), .pin2(n7432_6_pin5[15]), .pin3(n7408_3_pin3), .pin4(rom_1_data[1]),
    .pin5(n7404_1_pin10), .pin6(n7408_3_pin6), .pin13(rom_1_data[0]), .pin12(n7404_1_pin12),
    .pin11(n7408_3_pin11));  // open: pin10, pin9, pin8
  Adder #(.width(32)) adder_1 (
    .a({pc_q_4, pc_q_3, pc_q_2, pc_q}), .b(32'h1), .out(adder_1_out), .cin(1'b0));  // open: cout
  Register #(.width(32)) registerA (
    .D(multiplexer_2_out), .en(n7408_2_pin11), .clk(clk_out), .Q({registerA_q_2, registerA_q}),
    .clr(reset_out));
  Register #(.width(32)) registerM (
    .D(controlled_buffer_2_out), .en(n74175_1_pin2), .clk(clk_out), .Q(registerM_q), .clr(reset_out));
  Register #(.width(32)) registerD (
    .D(n7432_6_pin5), .en(n7408_2_pin3), .clk(clk_out), .Q(registerD_q), .clr(reset_out));
  assign bit_extender_1_out = {{31{n7404_1_pin4}}, n7404_1_pin4};  // Bit_Extender bit_extender_1
  assign bit_extender_2_out = {{31{rom_1_data[10]}}, rom_1_data[10]};  // Bit_Extender bit_extender_2
  assign bit_extender_3_out = {{31{n7404_1_pin6}}, n7404_1_pin6};  // Bit_Extender bit_extender_3
  assign bit_extender_4_out = {{31{rom_1_data[8]}}, rom_1_data[8]};  // Bit_Extender bit_extender_4
  assign bit_extender_5_out = {{31{rom_1_data[6]}}, rom_1_data[6]};  // Bit_Extender bit_extender_5
  _7432 u_7432_2 (
    .pin1(n7404_1_pin10), .pin2(n7432_6_pin5[15]), .pin3(n7404_1_pin13), .pin4(n7408_3_pin3),
    .pin5(n7408_3_pin6), .pin6(n7432_2_pin6), .pin10(n7408_3_pin11), .pin9(n7432_2_pin6), .pin8(n7408_1_pin2));  // open: pin13, pin12, pin11
  Multiplexer #(.width(32)) multiplexer_1 (
    .in0(adder_1_out), .in1({registerA_q_2, registerA_q}), .out(multiplexer_1_out), .sel(n7408_1_pin3));
  Multiplexer #(.width(32)) multiplexer_2 (
    .in0(rom_1_data), .in1(n7432_6_pin5), .out(multiplexer_2_out), .sel(rom_1_data[31]));
  Multiplexer #(.width(32)) multiplexer_3 (
    .in0({registerA_q_2, registerA_q}), .in1(registerM_q), .out(multiplexer_3_out), .sel(rom_1_data[12]));
  assign and_1_out = bit_extender_1_out & registerD_q;  // AND_Gate and_1, 32 bits wide
  assign and_2_out = bit_extender_3_out & multiplexer_3_out;  // AND_Gate and_2, 32 bits wide
  _7432 u_7432_3 (
    .pin1(n7432_3_pin1), .pin2(n7432_3_pin2), .pin3(n7432_3_pin3), .pin4(n7432_3_pin3), .pin5(n7432_3_pin5),
    .pin6(n7432_3_pin6), .pin13(n7432_3_pin13), .pin12(n7432_3_pin12), .pin11(n7432_3_pin5));  // open: pin10, pin9, pin8
  _7432 u_7432_4 (
    .pin1(n7432_4_pin1), .pin2(n7432_4_pin2), .pin3(n7432_4_pin3), .pin4(n7432_4_pin3), .pin5(n7432_3_pin6),
    .pin6(n7432_4_pin6), .pin13(n7432_4_pin13), .pin12(n7432_4_pin12), .pin11(n7432_4_pin11),
    .pin10(n7432_4_pin11), .pin9(n7432_4_pin6), .pin8(n7404_1_pin11));
  assign xor_1_out = and_1_out ^ bit_extender_2_out;  // XOR_Gate xor_1, 32 bits wide
  assign xor_2_out = and_2_out ^ bit_extender_4_out;  // XOR_Gate xor_2, 32 bits wide
  assign and_3_out = xor_1_out & xor_2_out;  // AND_Gate and_3, 32 bits wide
  Adder #(.width(32)) adder_2 (.a(xor_1_out), .b(xor_2_out), .out(adder_2_out), .cin(1'b0));  // open: cout
  _7432 u_7432_5 (
    .pin1(n7432_6_pin5[15]), .pin2(n7432_6_pin5[14]), .pin3(n7432_3_pin1), .pin4(n7432_6_pin5[9]),
    .pin5(n7432_6_pin5[8]), .pin6(n7432_3_pin2), .pin13(n7432_6_pin5[13]), .pin12(n7432_6_pin5[12]),
    .pin11(n7432_3_pin13), .pin10(n7432_6_pin5[11]), .pin9(n7432_6_pin5[10]), .pin8(n7432_3_pin12));
  _7432 u_7432_6 (
    .pin1(n7432_6_pin5[3]), .pin2(n7432_6_pin5[2]), .pin3(n7432_4_pin1), .pin4(n7432_6_pin5[1]),
    .pin5(n7432_6_pin5[0]), .pin6(n7432_4_pin2), .pin13(n7432_6_pin5[7]), .pin12(n7432_6_pin5[6]),
    .pin11(n7432_4_pin13), .pin10(n7432_6_pin5[5]), .pin9(n7432_6_pin5[4]), .pin8(n7432_4_pin12));
  Multiplexer #(.width(32)) multiplexer_4 (
    .in0(and_3_out), .in1(adder_2_out), .out(multiplexer_4_out), .sel(rom_1_data[7]));
  assign n7432_6_pin5 = multiplexer_4_out ^ bit_extender_5_out;  // XOR_Gate xor_3, 32 bits wide
  // also tied to VCC on the sheet: n74175_1_pin13

  // Notes on the sheet:
  //   contents of rom_1 (hex, n*v repeats v):
  //   3 ffffec10 a ffffe308 a fffffc98 4 ffffe301 3e8
endmodule
