// Logisim project CPU_logic.circ as structural Verilog: 1 circuit, main circuit main
module main (
);

  wire and_1_out, and_2_out, and_3_out, and_4_out, and_5_out, and_6_out, and_7_out, and_8_out, clk_out,
       d_ff_1_q, not_1_out, not_2_out, not_3_out, not_4_out, not_5_out, not_6_out, or_1_out, or_2_out,
       or_3_out, or_4_out, reset_out, stage_q, stage_qn;
  wire [7:0] pc_q, pc_q_2, pc_q_3, pc_q_4;
  wire [15:0] registerA_q, registerA_q_2;
  wire [31:0] adder_1_out, adder_2_out, and_9_out, and_10_out, and_11_out, bit_extender_1_out,
       bit_extender_2_out, bit_extender_3_out, bit_extender_4_out, bit_extender_5_out,
       controlled_buffer_2_out, multiplexer_1_out, multiplexer_2_out, multiplexer_3_out, multiplexer_4_out,
       ram_1_data, registerD_q, registerM_q, rom_1_data, xor_1_out, xor_2_out, xor_3_out;

  RAM #(.addrWidth(16), .clearpin("true"), .dataWidth(32), .databus("bidir")) ram_1 (
    .addr(registerA_q), .we(and_1_out), .oe(stage_q), .clk(not_1_out), .data(ram_1_data), .clr(reset_out));
  ROM #(.addrWidth(24), .dataWidth(32)) rom_1 (.addr({pc_q_3, pc_q_2, pc_q}), .data(rom_1_data));
  not not_1 (not_1_out, clk_out);
  and and_1 (and_1_out, stage_qn, rom_1_data[31], rom_1_data[3]);
  assign ram_1_data = stage_qn ? xor_3_out : 32'bz;  // Controlled_Buffer controlled_buffer_1
  and and_2 (and_2_out, rom_1_data[31], or_1_out);
  or or_1 (or_1_out, and_3_out, and_4_out, and_5_out);
  Clock clk (.out(clk_out));
  and and_3 (and_3_out, rom_1_data[2], xor_3_out[15]);
  and and_4 (and_4_out, rom_1_data[1], not_4_out);
  and and_5 (and_5_out, rom_1_data[0], not_3_out);
  T_Flip_Flop stage (.T(1'b1), .clk(clk_out), .Q(stage_q), .Qn(stage_qn), .reset(reset_out));  // open: preset
  not not_2 (not_2_out, rom_1_data[31]);
  not not_3 (not_3_out, or_3_out);
  and and_6 (and_6_out, stage_qn, d_ff_1_q);
  Button reset (.out(reset_out));
  or or_2 (or_2_out, not_2_out, rom_1_data[5]);
  or or_3 (or_3_out, not_4_out, xor_3_out[15]);
  D_Flip_Flop d_ff_1 (.D(1'b1), .clk(clk_out), .Q(d_ff_1_q), .reset(reset_out));  // open: Qn, preset
  not not_4 (not_4_out, or_4_out);
  or or_4 (or_4_out, xor_3_out[15], xor_3_out[14], xor_3_out[13], xor_3_out[12], xor_3_out[11], xor_3_out[10], xor_3_out[9], xor_3_out[8], xor_3_out[7], xor_3_out[6], xor_3_out[5], xor_3_out[4], xor_3_out[3], xor_3_out[2], xor_3_out[1], xor_3_out[0]);
  Register #(.width(32)) pc (
    .D(multiplexer_1_out), .en(and_6_out), .clk(clk_out), .Q({pc_q_4, pc_q_3, pc_q_2, pc_q}), .clr(reset_out));
  assign controlled_buffer_2_out = stage_q ? ram_1_data : 32'bz;  // Controlled_Buffer controlled_buffer_2
  and and_7 (and_7_out, stage_qn, or_2_out);
  and and_8 (and_8_out, rom_1_data[4], rom_1_data[31]);
  not not_5 (not_5_out, rom_1_data[11]);
  not not_6 (not_6_out, rom_1_data[9]);
  Adder #(.width(32)) adder_1 (
    .a({pc_q_4, pc_q_3, pc_q_2, pc_q}), .b(32'h1), .out(adder_1_out), .cin(1'b0));  // open: cout
  Register #(.width(32)) registerA (
    .D(multiplexer_2_out), .en(and_7_out), .clk(clk_out), .Q({registerA_q_2, registerA_q}), .clr(reset_out));
  Register #(.width(32)) registerM (
    .D(controlled_buffer_2_out), .en(stage_q), .clk(clk_out), .Q(registerM_q), .clr(reset_out));
  Register #(.width(32)) registerD (.D(xor_3_out), .en(and_8_out), .clk(clk_out), .Q(registerD_q), .clr(reset_out));
  assign bit_extender_1_out = {{31{not_5_out}}, not_5_out};  // Bit_Extender bit_extender_1
  assign bit_extender_2_out = {{31{rom_1_data[10]}}, rom_1_data[10]};  // Bit_Extender bit_extender_2
  assign bit_extender_3_out = {{31{not_6_out}}, not_6_out};  // Bit_Extender bit_extender_3
  assign bit_extender_4_out = {{31{rom_1_data[8]}}, rom_1_data[8]};  // Bit_Extender bit_extender_4
  assign bit_extender_5_out = {{31{rom_1_data[6]}}, rom_1_data[6]};  // Bit_Extender bit_extender_5
  Multiplexer #(.width(32)) multiplexer_1 (
    .in0(adder_1_out), .in1({registerA_q_2, registerA_q}), .out(multiplexer_1_out), .sel(and_2_out));
  Multiplexer #(.width(32)) multiplexer_2 (
    .in0(rom_1_data), .in1(xor_3_out), .out(multiplexer_2_out), .sel(rom_1_data[31]));
  Multiplexer #(.width(32)) multiplexer_3 (
    .in0({registerA_q_2, registerA_q}), .in1(registerM_q), .out(multiplexer_3_out), .sel(rom_1_data[12]));
  assign and_9_out = bit_extender_1_out & registerD_q;  // AND_Gate and_9, 32 bits wide
  assign and_10_out = bit_extender_3_out & multiplexer_3_out;  // AND_Gate and_10, 32 bits wide
  assign xor_1_out = and_9_out ^ bit_extender_2_out;  // XOR_Gate xor_1, 32 bits wide
  assign xor_2_out = and_10_out ^ bit_extender_4_out;  // XOR_Gate xor_2, 32 bits wide
  assign and_11_out = xor_1_out & xor_2_out;  // AND_Gate and_11, 32 bits wide
  Adder #(.width(32)) adder_2 (.a(xor_1_out), .b(xor_2_out), .out(adder_2_out), .cin(1'b0));  // open: cout
  Multiplexer #(.width(32)) multiplexer_4 (
    .in0(and_11_out), .in1(adder_2_out), .out(multiplexer_4_out), .sel(rom_1_data[7]));
  assign xor_3_out = multiplexer_4_out ^ bit_extender_5_out;  // XOR_Gate xor_3, 32 bits wide

  // Notes on the sheet:
  //   contents of rom_1 (hex, n*v repeats v):
  //   3 ffffec10 a ffffe308 a fffffc98 4 ffffe301 3e8
endmodule
