// Logisim project CPU_many_or_gates.circ as structural Verilog: 1 circuit, main circuit main
module main (
);

  wire and_1_out, and_6_out, and_8_out, bit_extender_1_out, clk_out, not_1_out, not_2_out, not_3_out,
       not_4_out, not_5_out, or_1_out, or_2_out, or_4_out, or_5_out, or_6_out, or_7_out, or_8_out, or_9_out,
       or_10_out, or_11_out, or_12_out, or_13_out, or_14_out, or_15_out, or_16_out, or_17_out, stage_qn;
  wire [15:0] registerA_q, registerA_q_2;
  wire [31:0] adder_1_out, and_7_out, and_9_out, and_10_out, and_11_out, bit_extender_2_out,
       bit_extender_3_out, bit_extender_4_out, bit_extender_5_out, bit_extender_6_out, bit_extender_7_out,
       multiplexer_1_out, multiplexer_2_out, multiplexer_3_out, ram_1_data, registerD_q, registerM_q,
       rom_1_data, undriven, xor_1_out, xor_2_out, xor_3_out;

  RAM #(.addrWidth(16), .dataWidth(32), .databus("bidir")) ram_1 (
    .addr(registerA_q), .we(and_1_out), .oe(stage_qn), .clk(clk_out), .data(ram_1_data));
  ROM #(.addrWidth(24), .dataWidth(32)) rom_1 (.data(rom_1_data));  // open: addr
  and and_1 (and_1_out, bit_extender_1_out, rom_1_data[3]);
  Clock clk (.out(clk_out));
  assign ram_1_data = xor_3_out & undriven;  // AND_Gate and_2, 32 bits wide
  Bit_Extender #(.in_width(32), .out_width(1)) bit_extender_1 (.in(undriven), .out(bit_extender_1_out));
  // AND_Gate and_3 has open pins: in0=rom_1_data[2], in1=xor_3_out[15], out=open
  // AND_Gate and_4 has open pins: in0=rom_1_data[0], in1=not_2_out, out=open
  // AND_Gate and_5 has open pins: in0=rom_1_data[1], in1=not_3_out, out=open
  T_Flip_Flop stage (.T(1'b1), .clk(clk_out), .Q(bit_extender_1_out), .Qn(stage_qn));  // open: reset, preset
  not not_1 (not_1_out, rom_1_data[31]);
  not not_2 (not_2_out, xor_3_out[15]);
  not not_3 (not_3_out, or_2_out);
  or or_1 (or_1_out, not_1_out, rom_1_data[5]);
  or or_2 (or_2_out, or_4_out, or_5_out);
  // OR_Gate or_3 is placed but not wired
  or or_4 (or_4_out, or_6_out, or_7_out);
  or or_5 (or_5_out, or_8_out, or_9_out);
  and and_6 (and_6_out, bit_extender_1_out, or_1_out);
  assign bit_extender_2_out = {{31{stage_qn}}, stage_qn};  // Bit_Extender bit_extender_2
  assign and_7_out = bit_extender_2_out & ram_1_data;  // AND_Gate and_7, 32 bits wide
  and and_8 (and_8_out, rom_1_data[4], rom_1_data[31]);
  or or_6 (or_6_out, or_10_out, or_11_out);
  or or_7 (or_7_out, or_12_out, or_13_out);
  or or_8 (or_8_out, or_14_out, or_15_out);
  or or_9 (or_9_out, or_16_out, or_17_out);
  not not_4 (not_4_out, rom_1_data[11]);
  not not_5 (not_5_out, rom_1_data[9]);
  or or_10 (or_10_out, xor_3_out[15], xor_3_out[14]);
  or or_11 (or_11_out, xor_3_out[13], xor_3_out[12]);
  or or_12 (or_12_out, xor_3_out[11], xor_3_out[10]);
  or or_13 (or_13_out, xor_3_out[9], xor_3_out[8]);
  or or_14 (or_14_out, xor_3_out[7], xor_3_out[6]);
  or or_15 (or_15_out, xor_3_out[5], xor_3_out[4]);
  or or_16 (or_16_out, xor_3_out[3], xor_3_out[2]);
  or or_17 (or_17_out, xor_3_out[1], xor_3_out[0]);
  Register #(.width(32)) registerA (
    .D(multiplexer_1_out), .en(and_6_out), .clk(clk_out), .Q({registerA_q_2, registerA_q}));  // open: clr
  Register #(.width(32)) registerM (.D(and_7_out), .en(stage_qn), .clk(clk_out), .Q(registerM_q));  // open: clr
  Register #(.width(32)) registerD (.D(xor_3_out), .en(and_8_out), .clk(clk_out), .Q(registerD_q));  // open: clr
  assign bit_extender_3_out = {{31{not_4_out}}, not_4_out};  // Bit_Extender bit_extender_3
  assign bit_extender_4_out = {{31{rom_1_data[10]}}, rom_1_data[10]};  // Bit_Extender bit_extender_4
  assign bit_extender_5_out = {{31{not_5_out}}, not_5_out};  // Bit_Extender bit_extender_5
  assign bit_extender_6_out = {{31{rom_1_data[8]}}, rom_1_data[8]};  // Bit_Extender bit_extender_6
  assign bit_extender_7_out = {{31{rom_1_data[6]}}, rom_1_data[6]};  // Bit_Extender bit_extender_7
  Multiplexer #(.width(32)) multiplexer_1 (
    .in0(rom_1_data), .in1(xor_3_out), .out(multiplexer_1_out), .sel(rom_1_data[31]));
  Multiplexer #(.width(32)) multiplexer_2 (
    .in0({registerA_q_2, registerA_q}), .in1(registerM_q), .out(multiplexer_2_out), .sel(rom_1_data[12]));
  assign and_9_out = bit_extender_3_out & registerD_q;  // AND_Gate and_9, 32 bits wide
  assign and_10_out = bit_extender_5_out & multiplexer_2_out;  // AND_Gate and_10, 32 bits wide
  Register #(.width(32)) pc ();  // open: D, en, clk, Q, clr
  assign xor_1_out = and_9_out ^ bit_extender_4_out;  // XOR_Gate xor_1, 32 bits wide
  assign xor_2_out = and_10_out ^ bit_extender_6_out;  // XOR_Gate xor_2, 32 bits wide
  Adder #(.width(32)) adder_1 (.a(xor_1_out), .b(xor_2_out), .out(adder_1_out));  // open: cin, cout
  assign and_11_out = xor_1_out & xor_2_out;  // AND_Gate and_11, 32 bits wide
  Multiplexer #(.width(32)) multiplexer_3 (
    .in0(adder_1_out), .in1(and_11_out), .out(multiplexer_3_out), .sel(rom_1_data[7]));
  assign xor_3_out = multiplexer_3_out ^ bit_extender_7_out;  // XOR_Gate xor_3, 32 bits wide
endmodule
